// Digital circuit tom-1.dig as structural Verilog
module tom_1 (
  input  clk,
  input  in_3,
  output clk_2
);

  wire and_1_out, and_2_out, and_3_out, and_4_out, d_ff_1_nq, decoder_1_out_0, decoder_1_out_1,
       decoder_1_out_2, decoder_1_out_3, delay_1_out, driver_1_out, nand_1_out, nclk, not_1_out, not_2_out,
       not_3_out, not_4_out, not_5_out, not_6_out, not_8_out, nreset, nstage, nTOS_eq__eq_0_nis0, stage,
       tom_269_1_ntc, xor_1_out;
  wire [7:0] CTRL_2_p4, D_REGISTER_q, PROGRAM_COUNTER_pc, PROGRAM_COUNTER_pc_2, tom_1_573_1_out,
       tom_1_573_2_out, TOS__HI_p4, TOS__LO_p4;
  wire [15:0] ROM_d, T2SB__HI_p4, TOS__HI_p1;
  wire [15:1] tom_269_2_q;

  // Probe TOS on {TOS__HI_p4, TOS__LO_p4}
  D_FF d_ff_1 (.D(1'b1), .C(clk), .nQ(d_ff_1_nq));  // open: Q
  SixteenSeg sixteenseg_1 (.led({TOS__HI_p4, TOS__LO_p4}), .dp(1'b0));
  Reset reset_1 (.out(nreset));
  not not_1 (not_1_out, clk);
  tom_1_is0 nTOS_eq__eq_0 (.\input ({TOS__HI_p4, TOS__LO_p4}), .nis0(nTOS_eq__eq_0_nis0));
  assign nclk = ~d_ff_1_nq ? not_1_out : 1'bz;  // DriverInvSel driverinvsel_1
  not not_2 (not_2_out, nTOS_eq__eq_0_nis0);
  assign clk_2 = ~d_ff_1_nq ? clk : 1'bz;  // DriverInvSel driverinvsel_2
  LED led_1 (.in(nclk));
  PullDown pulldown_1 (.out(nclk));
  PullDown pulldown_2 (.out(clk_2));
  not not_3 (not_3_out, ROM_d[9]);
  and and_1 (and_1_out, ROM_d[11], clk_2);
  Decoder #(.Selector_Bits(2)) decoder_1 (
    .sel(ROM_d[14:13]), .out_0(decoder_1_out_0), .out_1(decoder_1_out_1), .out_2(decoder_1_out_2),
    .out_3(decoder_1_out_3));
  and and_2 (and_2_out, not_2_out, clk_2, ROM_d[15]);
  LED led_2 (.in(clk_2));
  xor xor_1 (xor_1_out, nreset, and_2_out);
  // Probe CCK on and_1_out
  and and_3 (and_3_out, not_3_out, and_1_out);
  and and_4 (and_4_out, ROM_d[9], and_1_out);
  not not_4 (not_4_out, and_2_out);
  tom_1_pc PROGRAM_COUNTER (
    .clk(nclk), .\input ({CTRL_2_p4, ROM_d[7:0]}), .nLOAD(xor_1_out),
    .pc({PROGRAM_COUNTER_pc_2, PROGRAM_COUNTER_pc}));
  // tom_374 TOS__LO: pin names not known; wires that end beside it: TOS__HI_p1[7:0], ROM_d[8], nstage, TOS__LO_p4
  // tom_374 TOS__HI: pin names not known; wires that end beside it: TOS__HI_p1[15:8], ROM_d[8], nstage, TOS__HI_p4
  tom_1_d_r D_REGISTER (
    .nENP(1'b0), .nCCLR(nreset), .RCK(1'b0), .R_nC(1'b0), .nG(ROM_d[9]), .nLOAD(1'b1), .nENT(1'b0),
    .U_nD(ROM_d[10]), .D({8{1'b0}}), .CCK(and_3_out), .Q(D_REGISTER_q));
  tom_1_d_r R_REGISTER (
    .nENP(1'b0), .nCCLR(nreset), .RCK(1'b0), .R_nC(1'b0), .nG(not_3_out), .nLOAD(1'b1), .nENT(1'b0),
    .U_nD(ROM_d[10]), .D({8{1'b0}}), .CCK(and_4_out), .Q(D_REGISTER_q));
  Delay delay_1 (.in(not_4_out), .out(delay_1_out));
  // Probe dr on D_REGISTER_q
  tom_1_573 tom_1_573_1 (.C(nclk), .in(PROGRAM_COUNTER_pc), .out(tom_1_573_1_out));
  tom_1_573 tom_1_573_2 (.C(nclk), .in(PROGRAM_COUNTER_pc_2), .out(tom_1_573_2_out));
  tom_269 tom_269_1 (
    .nPE(delay_1_out), .U_nD(1'b1), .CP(nclk), .nCEP(1'b0), .nCET(1'b0), .D(ROM_d[7:0]),
    .Q({tom_269_2_q[7:1], stage}), .nTC(tom_269_1_ntc));
  tom_269 tom_269_2 (
    .nPE(delay_1_out), .U_nD(1'b1), .CP(nclk), .nCEP(tom_269_1_ntc), .nCET(1'b0), .D(CTRL_2_p4),
    .Q(tom_269_2_q[15:8]));  // open: nTC
  not not_5 (not_5_out, decoder_1_out_1);
  not not_6 (not_6_out, ROM_d[12]);
  not not_7 (nstage, stage);
  // Probe PC on {tom_269_2_q, stage}
  EEPROM #(.AddrBits(16), .isProgramMemory("true"), .Bits(16)) ROM (
    .A({tom_269_2_q, stage}), .CS(1'b1), .WE(1'b0), .OE(nreset), .D(ROM_d));
  // Probe on {tom_269_2_q[7:1], stage}
  // Probe on tom_269_1_ntc
  // Probe on tom_269_2_q[15:8]
  nand nand_1 (nand_1_out, not_5_out, ROM_d[12]);
  // Probe on {tom_269_2_q, stage}
  // Probe on {tom_1_573_2_out, tom_1_573_1_out}
  // Probe CTRL on ROM_d[15:8]
  // tom_1_373 T2SB__LO: pin names not known; wires that end beside it: TOS__LO_p4, nand_1_out, 1'b1, T2SB__HI_p4[7:0]
  // tom_1_373 T2SB__HI: pin names not known; wires that end beside it: TOS__HI_p4, nand_1_out, 1'b1, T2SB__HI_p4[15:8]
  RAMSinglePortSel #(.AddrBits(16), .Bits(16)) RAM (
    .A({TOS__HI_p4, TOS__LO_p4}), .CS(~not_5_out), .WE(~ROM_d[12]), .OE(~not_6_out), .D(T2SB__HI_p4));
  RAMSinglePortSel #(.AddrBits(9), .Bits(16)) STACK (
    .A({ROM_d[9], D_REGISTER_q}), .CS(~1'b0), .WE(~not_6_out), .OE(~ROM_d[12]), .D(T2SB__HI_p4));
  // tom_374 CTRL_2: pin names not known; wires that end beside it: ROM_d[7:0], 1'b0, stage, CTRL_2_p4
  not not_8 (not_8_out, decoder_1_out_0);
  // tom_1_373 R2TB__LO: pin names not known; wires that end beside it: ROM_d[7:0], not_8_out, 1'b1, TOS__HI_p1[7:0]
  // tom_1_373 R2TB__HI: pin names not known; wires that end beside it: CTRL_2_p4, not_8_out, 1'b1, TOS__HI_p1[15:8]
  // tom_1_add ADD: pin names not known; wires that end beside it: {TOS__HI_p4, TOS__LO_p4}, T2SB__HI_p4, decoder_1_out_2, TOS__HI_p1
  tom_1_nand NAND_2 (.A({TOS__HI_p4, TOS__LO_p4}), .B(T2SB__HI_p4), .enable(decoder_1_out_3), .out(TOS__HI_p1));
  // Probe ROM on {CTRL_2_p4, ROM_d[7:0]}
  // Probe tos_bus on TOS__HI_p1
  // Probe stack addr on {ROM_d[9], D_REGISTER_q}
  // Probe stack_bus on T2SB__HI_p4
  assign driver_1_out = in_3 ? nclk : 1'bz;  // Driver driver_1
  Break break_1 (.brk(driver_1_out));

  // Other names for the same wires on the sheet: clk_t = clk_2

  // Notes on the sheet:
  //   clk: Hz: 3
  //   in_3: default 1
  //   0 = TOS-DISABLE
  //   1 = DR-SEL
  //   2 = DR-UP
  //   3 = DR-CCK
  //   4 = STACK-WRITE
  //   5 = TOS-BUS-SEL-1
  //   6 = TOS-BUS-SEL-2
  //   7 = JUMPIF0
  //   TOMSCII
  //   573s needed until PC latching works
  //   stage (pc low bit)
  //   contents of ROM (hex, n*v repeats v):
  //   0,100,1cca,14fe,1c00,1410,2800,4100,1c00,1410,3c00,4900,800,4100,1c00,1400,800,8000,
  //   1c00,1401,800,8000
endmodule
